# Fritzing sketch peltier-schematic (saved by Fritzing 0.9.2b)

parts:
  TRINKET1 = Trinket 5V
  T1 = TMP36 Temperature Sensor [package="TO92 [THT]"]
  J1 = Peltier Element
  J2 = female pin header, 3 pins [form="♀ (female)"]
  J3 = male pin header, 3 pins [form="♂ (male)"]
  U1 = DC-DC_CONVERTER [package=dc-dc_converter]
  J5 = male pin header, 4 pins [form="♂ (male)"]
  J4 = female pin header, 4 pins [form="♀ (female)"]

nets:
  N1: TRINKET1.no_name_yet#2, J2.pin1, U1.GND1
  N2: TRINKET1.no_name_yet#6, J2.pin3, U1.VIN
  N3: TRINKET1.no_name_yet#7, J2.pin2
  N4: TRINKET1.no_name_yet#8, U1.ON_OFF
  N5: T1.+Vs, J3.pin3
  N6: T1.Vout, J3.pin2
  N7: T1.GND, J3.pin1
  N8: J1.pin1, J5.pin3, J5.pin4
  N9: J1.pin2, J5.pin1, J5.pin2
  N10: U1.VOUT, J4.pin1, J4.pin2
  N11: U1.GND2, J4.pin3, J4.pin4

custom parts:
  Trinket 5V: Adafruit Trinket 5V
